# Fritzing sketch schema_MIDI (saved by Fritzing 0.9.3b)
breadboards: 2

parts:
  Parte1 = Arduino Uno (Rev3) - ICSP
  R2 = Rotary Potentiometer (Large) [maximum_resistance=10kΩ package=THT]
  R3 = Rotary Potentiometer (Large) [maximum_resistance=10kΩ package=THT]
  R4 = Rotary Potentiometer (Large) [maximum_resistance=10kΩ package=THT]
  R1 = Rotary Potentiometer (Large) [maximum_resistance=10kΩ package=THT]
  LED1 = smd LED [color="Blue (430nm)" package="0805 [SMD]"]
  LED2 = smd LED [color="White (4500K)" package="0805 [SMD]"]
  LED3 = smd LED [color="Blue (430nm)" package="0805 [SMD]"]
  R5 = Resistor [tolerance=±5% resistance=1k package="2010 [SMD]"]
  R6 = Resistor [tolerance=±5% resistance=1k package="2010 [SMD]"]
  R7 = Resistor [tolerance=±5% resistance=1k package="2010 [SMD]"]
  S1 = Pushbutton [package="[SMD]"]
  S2 = Pushbutton [package="[SMD]"]
  S3 = Pushbutton [package="[SMD]"]
  S4 = Pushbutton [package="[SMD]"]
  S5 = Pushbutton [package="[SMD]"]
  S6 = Pushbutton [package="[SMD]"]
  S7 = Pushbutton [package="[SMD]"]
  S8 = Pushbutton [package="[SMD]"]
  R8 = Rotary Potentiometer (Large) [maximum_resistance=10kΩ package=THT]
  R9 = Rotary Potentiometer (Large) [maximum_resistance=10kΩ package=THT]

nets:
  N1: Parte1.A0, R4.wiper
  N2: Parte1.A1, R3.wiper
  N3: Parte1.A2, R2.wiper
  N4: Parte1.A3, R1.wiper
  N5: Parte1.A4/SDA, R9.wiper
  N6: Parte1.A5/SCL, R8.wiper
  N7: Parte1.ICSP_MISO, Parte1.D12/MISO, LED1.anode
  N8: Parte1.ICSP_MOSI, Parte1.D11_PWM/MOSI, LED2.anode
  N9: Parte1.D8, S8.Pin_3, S8.Pin_4
  N10: Parte1.D9_PWM, S1.Pin_1, S1.Pin_2
  N11: Parte1.D10_PWM/SS, LED3.anode
  N12: Parte1.D2, S2.Pin_3, S2.Pin_4
  N13: Parte1.D3_PWM, S3.Pin_3, S3.Pin_4
  N14: Parte1.D4, S4.Pin_3, S4.Pin_4
  N15: Parte1.D5_PWM, S5.Pin_3, S5.Pin_4
  N16: Parte1.D6_PWM, S6.Pin_3, S6.Pin_4
  N17: Parte1.D7, S7.Pin_3, S7.Pin_4
  N18: Parte1.5V, R2.leg1, R3.leg1, R4.leg1, R1.leg1, R8.leg1, R9.leg1
  N19: Parte1.GND, R2.leg2, R3.leg2, R4.leg2, R1.leg2, R5.Pin_1, R6.Pin_1, R7.Pin_1, S1.Pin_3, S1.Pin_4, S2.Pin_1, S2.Pin_2, S3.Pin_1, S3.Pin_2, S4.Pin_1, S4.Pin_2, S5.Pin_1, S5.Pin_2, S6.Pin_1, S6.Pin_2, S7.Pin_1, S7.Pin_2, S8.Pin_1, S8.Pin_2, R8.leg2, R9.leg2
  N20: LED1.cathode, R5.Pin_0
  N21: LED2.cathode, R6.Pin_0
  N22: LED3.cathode, R7.Pin_0
